// Logisim project divisor(1).circ as structural Verilog: 3 circuits, main circuit main
module main (
  input  a,
  input  b,
  input  c,
  output y
);

  wire xor_1_out;

  xor xor_1 (xor_1_out, b, c);
  xor xor_2 (y, xor_1_out, a);
endmodule

module somador (
  input  [7:0] in_1,
  input  [7:0] in_2,
  input  in_3,
  output [7:0] out_4,
  output out_5
);

  wire and_1_out, and_2_out, and_3_out, and_4_out, and_5_out, and_6_out, and_7_out, and_8_out, and_9_out,
       and_10_out, and_11_out, and_12_out, and_13_out, and_14_out, and_15_out, and_16_out, and_17_out,
       and_18_out, and_19_out, and_20_out, and_21_out, and_22_out, and_23_out, and_24_out, and_25_out,
       and_26_out, and_27_out, and_28_out, and_29_out, and_30_out, and_31_out, and_32_out, and_33_out,
       and_34_out, and_35_out, or_1_out, or_2_out, or_3_out, or_4_out, or_5_out, or_6_out, or_7_out,
       or_8_out, or_9_out, or_10_out, or_11_out, or_12_out, or_13_out, or_14_out;
  wire [7:0] xor_1_out;

  assign xor_1_out = in_2 ^ {8{in_3}};  // XOR_Gate xor_1, 8 bits wide
  main main_1 (.a(xor_1_out[0]), .b(in_1[0]), .c(in_3), .y(out_4[0]));
  and and_1 (and_1_out, in_1[0], xor_1_out[0]);
  or or_1 (or_1_out, in_1[0], xor_1_out[0]);
  and and_2 (and_2_out, or_1_out, in_3);
  or or_2 (or_2_out, and_1_out, and_2_out);
  main main_2 (.a(xor_1_out[1]), .b(in_1[1]), .c(or_2_out), .y(out_4[1]));
  and and_3 (and_3_out, in_1[1], xor_1_out[1]);
  and and_4 (and_4_out, and_1_out, or_4_out);
  or or_3 (or_3_out, and_3_out, and_4_out, and_5_out);
  main main_3 (.a(xor_1_out[2]), .b(in_1[2]), .c(or_3_out), .y(out_4[2]));
  or or_4 (or_4_out, in_1[1], xor_1_out[1]);
  and and_5 (and_5_out, or_1_out, or_4_out, in_3);
  main main_4 (.a(xor_1_out[3]), .b(in_1[3]), .c(or_6_out), .y(out_4[3]));
  or or_5 (or_5_out, in_1[2], xor_1_out[2]);
  and and_6 (and_6_out, in_1[2], xor_1_out[2]);
  and and_7 (and_7_out, and_1_out, or_4_out, or_5_out);
  and and_8 (and_8_out, and_3_out, or_5_out);
  or or_6 (or_6_out, and_6_out, and_8_out, and_7_out, and_9_out);
  and and_9 (and_9_out, in_3, or_1_out, or_4_out, or_5_out);
  main main_5 (.a(xor_1_out[4]), .b(in_1[4]), .c(or_8_out), .y(out_4[4]));
  or or_7 (or_7_out, in_1[3], xor_1_out[3]);
  and and_10 (and_10_out, in_1[3], xor_1_out[3]);
  and and_11 (and_11_out, and_6_out, or_7_out);
  and and_12 (and_12_out, and_3_out, or_5_out, or_7_out);
  or or_8 (or_8_out, and_10_out, and_11_out, and_12_out, and_13_out, and_14_out);
  and and_13 (and_13_out, and_1_out, and_3_out, and_6_out, or_7_out);
  and and_14 (and_14_out, in_3, or_1_out, or_4_out, or_5_out, or_7_out);
  and and_15 (and_15_out, in_1[4], xor_1_out[4]);
  and and_16 (and_16_out, and_10_out, or_9_out);
  main main_6 (.a(xor_1_out[5]), .b(in_1[5]), .c(or_10_out), .y(out_4[5]));
  or or_9 (or_9_out, in_1[4], xor_1_out[4]);
  and and_17 (and_17_out, and_3_out, or_5_out, or_7_out, or_9_out);
  and and_18 (and_18_out, and_6_out, or_7_out, or_9_out);
  or or_10 (or_10_out, and_15_out, and_16_out, and_18_out, and_17_out, and_19_out, and_20_out);
  and and_19 (and_19_out, and_1_out, and_3_out, and_6_out, and_10_out, and_15_out);
  and and_20 (and_20_out, in_3, or_1_out, or_4_out, or_5_out, or_7_out, or_9_out);
  main main_7 (.a(xor_1_out[6]), .b(in_1[6]), .c(or_12_out), .y(out_4[6]));
  or or_11 (or_11_out, in_1[5], xor_1_out[5]);
  and and_21 (and_21_out, in_1[5], xor_1_out[5]);
  and and_22 (and_22_out, and_15_out, or_11_out);
  and and_23 (and_23_out, and_10_out, or_9_out, or_11_out);
  or or_12 (or_12_out, and_21_out, and_22_out, and_23_out, and_24_out, and_25_out, and_26_out, and_27_out);
  and and_24 (and_24_out, and_6_out, or_7_out, or_9_out, or_11_out);
  and and_25 (and_25_out, and_3_out, or_5_out, or_7_out, or_9_out, or_11_out);
  and and_26 (and_26_out, and_1_out, and_3_out, and_6_out, and_10_out, and_15_out, and_21_out);
  and and_27 (and_27_out, in_3, or_1_out, or_4_out, or_5_out, or_7_out, or_9_out, or_11_out);
  or or_13 (or_13_out, in_1[6], xor_1_out[6]);
  and and_28 (and_28_out, in_1[6], xor_1_out[6]);
  and and_29 (and_29_out, and_21_out, or_13_out);
  main main_8 (.a(xor_1_out[7]), .b(in_1[7]), .c(or_14_out), .y(out_4[7]));
  and and_30 (and_30_out, and_10_out, or_9_out, or_11_out, or_13_out);
  and and_31 (and_31_out, and_15_out, or_11_out, or_13_out);
  or or_14 (or_14_out, and_28_out, and_29_out, and_31_out, and_30_out, and_32_out, and_33_out, and_34_out, and_35_out);
  and and_32 (and_32_out, and_6_out, or_7_out, or_9_out, or_11_out, or_13_out);
  and and_33 (and_33_out, and_3_out, and_6_out, and_10_out, and_15_out, and_21_out, and_28_out);
  and and_34 (and_34_out, and_3_out, and_3_out, or_5_out, or_7_out, or_9_out, or_11_out, or_13_out);
  and and_35 (and_35_out, in_3, or_1_out, or_4_out, or_5_out, or_7_out, or_9_out, or_11_out, or_13_out);

  assign out_5 = out_4[7];
endmodule

module main_2 (
  input  [7:0] in_1,
  input  [7:0] in_2,
  output [7:0] out_3,
  output [7:0] out_4
);

  wire s0, s1, s2, s3, s4, s5, s6, s7;
  wire [7:0] multiplexer_1_out, multiplexer_2_out, multiplexer_3_out, multiplexer_4_out, multiplexer_5_out,
       multiplexer_6_out, multiplexer_7_out, somador_1_out_4, somador_2_out_4, somador_3_out_4,
       somador_4_out_4, somador_5_out_4, somador_6_out_4, somador_7_out_4, somador_8_out_4;

  somador somador_1 (.in_3(1'b1), .out_5(s7), .in_1({{7{1'b0}}, in_2[7]}), .in_2(in_1), .out_4(somador_1_out_4));
  Multiplexer #(.width(8)) multiplexer_1 (
    .in0(somador_1_out_4), .in1({{7{1'b0}}, in_2[7]}), .out(multiplexer_1_out), .sel(s7));  // open: en
  not not_1 (out_4[6], s6);
  not not_2 (out_4[3], s3);
  not not_3 (out_4[7], s7);
  not not_4 (out_4[5], s5);
  not not_5 (out_4[4], s4);
  somador somador_2 (
    .in_3(1'b1), .out_5(s6), .in_1({multiplexer_1_out[6:0], in_2[6]}), .in_2(in_1), .out_4(somador_2_out_4));
  not not_6 (out_4[0], s0);
  not not_7 (out_4[1], s1);
  not not_8 (out_4[2], s2);
  Multiplexer #(.width(8)) multiplexer_2 (
    .in0(somador_2_out_4), .in1({multiplexer_1_out[6:0], in_2[6]}), .out(multiplexer_2_out), .sel(s6));  // open: en
  somador somador_3 (
    .in_3(1'b1), .out_5(s5), .in_1({multiplexer_2_out[6:0], in_2[5]}), .in_2(in_1), .out_4(somador_3_out_4));
  Multiplexer #(.width(8)) multiplexer_3 (
    .in0(somador_3_out_4), .in1({multiplexer_2_out[6:0], in_2[5]}), .out(multiplexer_3_out), .sel(s5));  // open: en
  somador somador_4 (
    .in_3(1'b1), .out_5(s4), .in_1({multiplexer_3_out[6:0], in_2[4]}), .in_2(in_1), .out_4(somador_4_out_4));
  Multiplexer #(.width(8)) multiplexer_4 (
    .in0(somador_4_out_4), .in1({multiplexer_3_out[6:0], in_2[4]}), .out(multiplexer_4_out), .sel(s4));  // open: en
  somador somador_5 (
    .in_3(1'b1), .out_5(s3), .in_1({multiplexer_4_out[6:0], in_2[3]}), .in_2(in_1), .out_4(somador_5_out_4));
  Multiplexer #(.width(8)) multiplexer_5 (
    .in0(somador_5_out_4), .in1({multiplexer_4_out[6:0], in_2[3]}), .out(multiplexer_5_out), .sel(s3));  // open: en
  somador somador_6 (
    .in_3(1'b1), .out_5(s2), .in_1({multiplexer_5_out[6:0], in_2[2]}), .in_2(in_1), .out_4(somador_6_out_4));
  Multiplexer #(.width(8)) multiplexer_6 (
    .in0(somador_6_out_4), .in1({multiplexer_5_out[6:0], in_2[2]}), .out(multiplexer_6_out), .sel(s2));  // open: en
  somador somador_7 (
    .in_3(1'b1), .out_5(s1), .in_1({multiplexer_6_out[6:0], in_2[1]}), .in_2(in_1), .out_4(somador_7_out_4));
  Multiplexer #(.width(8)) multiplexer_7 (
    .in0(somador_7_out_4), .in1({multiplexer_6_out[6:0], in_2[1]}), .out(multiplexer_7_out), .sel(s1));  // open: en
  somador somador_8 (
    .in_3(1'b1), .out_5(s0), .in_1({multiplexer_7_out[6:0], in_2[0]}), .in_2(in_1), .out_4(somador_8_out_4));
  Multiplexer #(.width(8)) multiplexer_8 (
    .in0(somador_8_out_4), .in1({multiplexer_7_out[6:0], in_2[0]}), .out(out_3), .sel(s0));  // open: en

  // Other names for the same wires on the sheet: dividendo[7:0] = in_2; divisor[7:0] = in_1; quociente[7:0] = out_4;
  //   saida[7:0] = out_3
endmodule
