// Logisim project multiplicaDORes.circ as structural Verilog: 3 circuits, main circuit main
module main (
  input  [7:0] in_1,
  input  [7:0] in_2,
  output [7:0] out_3
);

  wire and_1_out, and_2_out, and_3_out, and_4_out, and_5_out, and_6_out, and_7_out, and_8_out, and_9_out,
       and_10_out, and_11_out, and_12_out, and_13_out, and_14_out, and_15_out, and_16_out, and_17_out,
       and_18_out, and_19_out, and_20_out, and_21_out, and_22_out, and_23_out, and_24_out, and_25_out,
       and_26_out, and_27_out, and_28_out, and_29_out, and_30_out, and_31_out, and_32_out, and_33_out,
       and_34_out, and_35_out, and_36_out, and_37_out, and_38_out, and_39_out, and_40_out, and_41_out,
       and_42_out, and_43_out, and_44_out, and_45_out, and_46_out, and_47_out, and_48_out, and_49_out,
       and_50_out, and_51_out, and_52_out, and_53_out, and_54_out, and_55_out, and_56_out, and_57_out,
       and_58_out, and_59_out, and_60_out, and_61_out, and_62_out, and_63_out, full_adder_1_cout,
       full_adder_1_s, full_adder_2_cout, full_adder_2_s, full_adder_3_cout, full_adder_3_s,
       full_adder_4_cout, full_adder_4_s, full_adder_5_cout, full_adder_5_s, full_adder_6_cout,
       full_adder_6_s, full_adder_7_cout, full_adder_7_s, full_adder_8_cout, full_adder_8_s,
       full_adder_9_cout, full_adder_9_s, full_adder_10_cout, full_adder_10_s, full_adder_11_cout,
       full_adder_11_s, full_adder_12_cout, full_adder_12_s, full_adder_13_cout, full_adder_13_s,
       full_adder_14_cout, full_adder_14_s, full_adder_15_cout, full_adder_15_s, full_adder_16_cout,
       full_adder_16_s, full_adder_17_cout, full_adder_17_s, full_adder_18_cout, full_adder_18_s,
       full_adder_19_cout, full_adder_19_s, full_adder_20_cout, full_adder_20_s, full_adder_21_cout,
       full_adder_21_s, full_adder_22_cout, full_adder_22_s, full_adder_23_cout, full_adder_23_s,
       full_adder_24_cout, full_adder_24_s, full_adder_25_cout, full_adder_25_s, full_adder_26_cout,
       full_adder_26_s, full_adder_27_cout, full_adder_27_s, full_adder_28_cout, full_adder_28_s,
       full_adder_29_cout, full_adder_29_s, full_adder_30_cout, full_adder_30_s, full_adder_31_cout,
       full_adder_31_s, full_adder_32_cout, full_adder_32_s, full_adder_33_cout, full_adder_33_s,
       full_adder_34_cout, full_adder_34_s, full_adder_35_cout, full_adder_35_s, full_adder_36_cout,
       full_adder_36_s, full_adder_37_cout, full_adder_37_s, full_adder_38_cout, full_adder_38_s,
       full_adder_39_cout, full_adder_39_s, full_adder_40_cout, full_adder_40_s, full_adder_41_cout,
       full_adder_41_s, full_adder_42_cout, full_adder_42_s, full_adder_43_cout, full_adder_43_s,
       full_adder_44_cout, full_adder_44_s, full_adder_45_cout, full_adder_45_s, full_adder_46_cout,
       full_adder_46_s, full_adder_47_cout, full_adder_47_s, full_adder_48_cout, full_adder_48_s,
       half_adder_1_cout, half_adder_1_s, half_adder_2_cout, half_adder_3_cout, half_adder_4_cout,
       half_adder_5_cout, half_adder_6_cout, half_adder_7_cout, half_adder_8_cout;
  wire [3:3] undriven;

  and and_1 (and_1_out, in_1[7], in_2[7]);
  Full_adder full_adder_1 (
    .a(and_1_out), .b(full_adder_2_cout), .cin(full_adder_3_cout), .s(full_adder_1_s),
    .cout(full_adder_1_cout));
  and and_2 (and_2_out, in_1[7], in_2[6]);
  Full_adder full_adder_2 (
    .a(and_2_out), .b(full_adder_4_cout), .cin(full_adder_5_cout), .s(full_adder_2_s),
    .cout(full_adder_2_cout));
  and and_3 (and_3_out, in_1[6], in_2[7]);
  Full_adder full_adder_3 (
    .a(and_3_out), .b(full_adder_2_s), .cin(full_adder_6_cout), .s(full_adder_3_s), .cout(full_adder_3_cout));
  Hex_Digit_Display hex_digit_display_1 (.value({undriven[3], in_1[2:0]}));  // open: dp
  Hex_Digit_Display hex_digit_display_2 (.value({1'b0, in_2[2:0]}));  // open: dp
  and and_4 (and_4_out, in_1[7], in_2[4]);
  and and_5 (and_5_out, in_1[7], in_2[5]);
  and and_6 (and_6_out, in_1[6], in_2[5]);
  Full_adder full_adder_4 (
    .a(and_5_out), .b(full_adder_7_cout), .cin(full_adder_8_cout), .s(full_adder_4_s),
    .cout(full_adder_4_cout));
  and and_7 (and_7_out, in_1[6], in_2[6]);
  Full_adder full_adder_5 (
    .a(and_7_out), .b(full_adder_4_s), .cin(full_adder_9_cout), .s(full_adder_5_s), .cout(full_adder_5_cout));
  and and_8 (and_8_out, in_1[5], in_2[7]);
  Full_adder full_adder_6 (
    .a(and_8_out), .b(full_adder_5_s), .cin(full_adder_10_cout), .s(full_adder_6_s), .cout(full_adder_6_cout));
  and and_9 (and_9_out, in_1[7], in_2[3]);
  and and_10 (and_10_out, in_1[6], in_2[4]);
  Full_adder full_adder_7 (
    .a(and_4_out), .b(full_adder_12_cout), .cin(full_adder_15_cout), .s(full_adder_7_s),
    .cout(full_adder_7_cout));
  and and_11 (and_11_out, in_1[5], in_2[5]);
  Full_adder full_adder_8 (
    .a(and_6_out), .b(full_adder_7_s), .cin(full_adder_17_cout), .s(full_adder_8_s), .cout(full_adder_8_cout));
  and and_12 (and_12_out, in_1[4], in_2[6]);
  and and_13 (and_13_out, in_1[5], in_2[6]);
  Full_adder full_adder_9 (
    .a(and_13_out), .b(full_adder_8_s), .cin(full_adder_18_cout), .s(full_adder_9_s), .cout(full_adder_9_cout));
  and and_14 (and_14_out, in_1[4], in_2[7]);
  and and_15 (and_15_out, in_1[3], in_2[7]);
  Full_adder full_adder_10 (
    .a(and_14_out), .b(full_adder_9_s), .cin(full_adder_19_cout), .s(full_adder_10_s),
    .cout(full_adder_10_cout));
  and and_16 (and_16_out, in_1[7], in_2[2]);
  Full_adder full_adder_11 (
    .a(and_16_out), .b(half_adder_1_cout), .cin(full_adder_20_cout), .s(full_adder_11_s),
    .cout(full_adder_11_cout));
  and and_17 (and_17_out, in_1[6], in_2[3]);
  Full_adder full_adder_12 (
    .a(and_9_out), .b(full_adder_11_cout), .cin(full_adder_13_cout), .s(full_adder_12_s),
    .cout(full_adder_12_cout));
  Full_adder full_adder_13 (
    .a(and_17_out), .b(full_adder_11_s), .cin(full_adder_21_cout), .s(full_adder_13_s),
    .cout(full_adder_13_cout));
  and and_18 (and_18_out, in_1[5], in_2[4]);
  Full_adder full_adder_14 (
    .a(and_18_out), .b(full_adder_13_s), .cin(full_adder_22_cout), .s(full_adder_14_s),
    .cout(full_adder_14_cout));
  Full_adder full_adder_15 (
    .a(and_10_out), .b(full_adder_12_s), .cin(full_adder_14_cout), .s(full_adder_15_s),
    .cout(full_adder_15_cout));
  and and_19 (and_19_out, in_1[4], in_2[5]);
  Full_adder full_adder_16 (
    .a(and_19_out), .b(full_adder_14_s), .cin(full_adder_23_cout), .s(full_adder_16_s),
    .cout(full_adder_16_cout));
  Full_adder full_adder_17 (
    .a(and_11_out), .b(full_adder_15_s), .cin(full_adder_16_cout), .s(full_adder_17_s),
    .cout(full_adder_17_cout));
  and and_20 (and_20_out, in_1[3], in_2[6]);
  Full_adder full_adder_18 (
    .a(and_12_out), .b(full_adder_17_s), .cin(full_adder_24_cout), .s(full_adder_18_s),
    .cout(full_adder_18_cout));
  and and_21 (and_21_out, in_1[2], in_2[7]);
  Full_adder full_adder_19 (
    .a(and_15_out), .b(full_adder_18_s), .cin(full_adder_26_cout), .s(full_adder_19_s),
    .cout(full_adder_19_cout));
  and and_22 (and_22_out, in_1[7], in_2[1]);
  half_adder half_adder_1 (.a(and_22_out), .b(full_adder_28_cout), .s(half_adder_1_s), .cout(half_adder_1_cout));
  and and_23 (and_23_out, in_1[6], in_2[2]);
  Full_adder full_adder_20 (
    .a(and_23_out), .b(half_adder_1_s), .cin(full_adder_29_cout), .s(full_adder_20_s),
    .cout(full_adder_20_cout));
  and and_24 (and_24_out, in_1[5], in_2[3]);
  Full_adder full_adder_21 (
    .a(and_24_out), .b(full_adder_20_s), .cin(full_adder_30_cout), .s(full_adder_21_s),
    .cout(full_adder_21_cout));
  and and_25 (and_25_out, in_1[4], in_2[4]);
  Full_adder full_adder_22 (
    .a(and_25_out), .b(full_adder_21_s), .cin(full_adder_31_cout), .s(full_adder_22_s),
    .cout(full_adder_22_cout));
  and and_26 (and_26_out, in_1[3], in_2[5]);
  Full_adder full_adder_23 (
    .a(and_26_out), .b(full_adder_22_s), .cin(full_adder_32_cout), .s(full_adder_23_s),
    .cout(full_adder_23_cout));
  and and_27 (and_27_out, in_1[2], in_2[6]);
  Full_adder full_adder_24 (
    .a(and_20_out), .b(full_adder_16_s), .cin(full_adder_25_cout), .s(full_adder_24_s),
    .cout(full_adder_24_cout));
  Full_adder full_adder_25 (
    .a(and_27_out), .b(full_adder_23_s), .cin(full_adder_33_cout), .s(full_adder_25_s),
    .cout(full_adder_25_cout));
  and and_28 (and_28_out, in_1[1], in_2[7]);
  Full_adder full_adder_26 (
    .a(and_21_out), .b(full_adder_24_s), .cin(full_adder_27_cout), .s(full_adder_26_s),
    .cout(full_adder_26_cout));
  Full_adder full_adder_27 (
    .a(and_28_out), .b(full_adder_25_s), .cin(half_adder_2_cout), .s(full_adder_27_s),
    .cout(full_adder_27_cout));
  and and_29 (and_29_out, in_1[7], in_2[0]);
  and and_30 (and_30_out, in_1[6], in_2[1]);
  Full_adder full_adder_28 (
    .a(and_30_out), .b(and_29_out), .cin(full_adder_34_cout), .s(full_adder_28_s), .cout(full_adder_28_cout));
  and and_31 (and_31_out, in_1[5], in_2[2]);
  Full_adder full_adder_29 (
    .a(and_31_out), .b(full_adder_28_s), .cin(full_adder_35_cout), .s(full_adder_29_s),
    .cout(full_adder_29_cout));
  and and_32 (and_32_out, in_1[4], in_2[3]);
  Full_adder full_adder_30 (
    .a(and_32_out), .b(full_adder_29_s), .cin(full_adder_36_cout), .s(full_adder_30_s),
    .cout(full_adder_30_cout));
  and and_33 (and_33_out, in_1[3], in_2[4]);
  Full_adder full_adder_31 (
    .a(and_33_out), .b(full_adder_30_s), .cin(full_adder_37_cout), .s(full_adder_31_s),
    .cout(full_adder_31_cout));
  and and_34 (and_34_out, in_1[2], in_2[5]);
  Full_adder full_adder_32 (
    .a(and_34_out), .b(full_adder_31_s), .cin(full_adder_38_cout), .s(full_adder_32_s),
    .cout(full_adder_32_cout));
  and and_35 (and_35_out, in_1[1], in_2[6]);
  Full_adder full_adder_33 (
    .a(and_35_out), .b(full_adder_32_s), .cin(half_adder_3_cout), .s(full_adder_33_s),
    .cout(full_adder_33_cout));
  and and_36 (and_36_out, in_1[0], in_2[7]);
  half_adder half_adder_2 (.a(and_36_out), .b(full_adder_33_s), .s(out_3[7]), .cout(half_adder_2_cout));
  and and_37 (and_37_out, in_1[6], in_2[0]);
  and and_38 (and_38_out, in_1[5], in_2[1]);
  Full_adder full_adder_34 (
    .a(and_38_out), .b(and_37_out), .cin(full_adder_39_cout), .s(full_adder_34_s), .cout(full_adder_34_cout));
  and and_39 (and_39_out, in_1[4], in_2[2]);
  Full_adder full_adder_35 (
    .a(and_39_out), .b(full_adder_34_s), .cin(full_adder_40_cout), .s(full_adder_35_s),
    .cout(full_adder_35_cout));
  and and_40 (and_40_out, in_1[3], in_2[3]);
  Full_adder full_adder_36 (
    .a(and_40_out), .b(full_adder_35_s), .cin(full_adder_41_cout), .s(full_adder_36_s),
    .cout(full_adder_36_cout));
  and and_41 (and_41_out, in_1[2], in_2[4]);
  Full_adder full_adder_37 (
    .a(and_41_out), .b(full_adder_36_s), .cin(full_adder_42_cout), .s(full_adder_37_s),
    .cout(full_adder_37_cout));
  and and_42 (and_42_out, in_1[1], in_2[5]);
  Full_adder full_adder_38 (
    .a(and_42_out), .b(full_adder_37_s), .cin(half_adder_4_cout), .s(full_adder_38_s),
    .cout(full_adder_38_cout));
  and and_43 (and_43_out, in_1[0], in_2[6]);
  half_adder half_adder_3 (.a(and_43_out), .b(full_adder_38_s), .s(out_3[6]), .cout(half_adder_3_cout));
  and and_44 (and_44_out, in_1[5], in_2[0]);
  and and_45 (and_45_out, in_1[4], in_2[0]);
  and and_46 (and_46_out, in_1[3], in_2[1]);
  and and_47 (and_47_out, in_1[4], in_2[1]);
  Full_adder full_adder_39 (
    .a(and_47_out), .b(and_44_out), .cin(full_adder_43_cout), .s(full_adder_39_s), .cout(full_adder_39_cout));
  and and_48 (and_48_out, in_1[3], in_2[2]);
  and and_49 (and_49_out, in_1[2], in_2[2]);
  Full_adder full_adder_40 (
    .a(and_48_out), .b(full_adder_39_s), .cin(full_adder_44_cout), .s(full_adder_40_s),
    .cout(full_adder_40_cout));
  and and_50 (and_50_out, in_1[2], in_2[3]);
  Full_adder full_adder_41 (
    .a(and_50_out), .b(full_adder_40_s), .cin(full_adder_45_cout), .s(full_adder_41_s),
    .cout(full_adder_41_cout));
  and and_51 (and_51_out, in_1[1], in_2[4]);
  Full_adder full_adder_42 (
    .a(and_51_out), .b(full_adder_41_s), .cin(half_adder_5_cout), .s(full_adder_42_s),
    .cout(full_adder_42_cout));
  and and_52 (and_52_out, in_1[0], in_2[5]);
  half_adder half_adder_4 (.a(and_52_out), .b(full_adder_42_s), .s(out_3[5]), .cout(half_adder_4_cout));
  and and_53 (and_53_out, in_1[3], in_2[0]);
  and and_54 (and_54_out, in_1[2], in_2[1]);
  Full_adder full_adder_43 (
    .a(and_46_out), .b(and_45_out), .cin(full_adder_47_cout), .s(full_adder_43_s), .cout(full_adder_43_cout));
  and and_55 (and_55_out, in_1[1], in_2[2]);
  Full_adder full_adder_44 (
    .a(and_49_out), .b(full_adder_43_s), .cin(full_adder_48_cout), .s(full_adder_44_s),
    .cout(full_adder_44_cout));
  and and_56 (and_56_out, in_1[0], in_2[3]);
  and and_57 (and_57_out, in_1[1], in_2[3]);
  Full_adder full_adder_45 (
    .a(and_57_out), .b(full_adder_44_s), .cin(half_adder_7_cout), .s(full_adder_45_s),
    .cout(full_adder_45_cout));
  and and_58 (and_58_out, in_1[0], in_2[4]);
  half_adder half_adder_5 (.a(and_58_out), .b(full_adder_45_s), .s(out_3[4]), .cout(half_adder_5_cout));
  and and_59 (and_59_out, in_1[2], in_2[0]);
  and and_60 (and_60_out, in_1[1], in_2[1]);
  Full_adder full_adder_46 (
    .a(and_60_out), .b(and_59_out), .cin(half_adder_8_cout), .s(full_adder_46_s), .cout(full_adder_46_cout));
  Full_adder full_adder_47 (
    .a(and_54_out), .b(and_53_out), .cin(full_adder_46_cout), .s(full_adder_47_s), .cout(full_adder_47_cout));
  and and_61 (and_61_out, in_1[0], in_2[2]);
  half_adder half_adder_6 (.a(and_61_out), .b(full_adder_46_s), .s(out_3[2]), .cout(half_adder_6_cout));
  Full_adder full_adder_48 (
    .a(and_55_out), .b(full_adder_47_s), .cin(half_adder_6_cout), .s(full_adder_48_s),
    .cout(full_adder_48_cout));
  half_adder half_adder_7 (.a(and_56_out), .b(full_adder_48_s), .s(out_3[3]), .cout(half_adder_7_cout));
  and and_62 (and_62_out, in_1[1], in_2[0]);
  and and_63 (and_63_out, in_1[0], in_2[1]);
  half_adder half_adder_8 (.a(and_63_out), .b(and_62_out), .s(out_3[1]), .cout(half_adder_8_cout));
  and and_64 (out_3[0], in_1[0], in_2[0]);

  // Other names for the same wires on the sheet: a0 = in_1[0]; a1 = in_1[1]; a2 = in_1[2]; a3 = in_1[3]; a4 = in_1[4];
  //   a5 = in_1[5]; a6 = in_1[6]; a7 = in_1[7]; b0 = in_2[0]; b1 = in_2[1]; b2 = in_2[2]; b3 = in_2[3]; b4 = in_2[4];
  //   b5 = in_2[5]; b6 = in_2[6]; b7 = in_2[7]
endmodule

module Full_adder (
  input  a,
  input  b,
  input  cin,
  output s,
  output cout
);

  wire and_1_out, and_2_out, and_3_out, and_4_out, and_5_out, and_6_out, and_7_out, not_1_out, not_2_out,
       not_3_out, not_4_out, not_5_out, not_6_out;

  not not_1 (not_1_out, a);
  not not_2 (not_2_out, b);
  not not_3 (not_3_out, a);
  not not_4 (not_4_out, cin);
  not not_5 (not_5_out, b);
  not not_6 (not_6_out, cin);
  and and_1 (and_1_out, b, cin);
  and and_2 (and_2_out, a, cin);
  and and_3 (and_3_out, a, b);
  and and_4 (and_4_out, not_1_out, not_2_out, cin);
  and and_5 (and_5_out, not_3_out, b, not_4_out);
  and and_6 (and_6_out, a, not_5_out, not_6_out);
  and and_7 (and_7_out, a, b, cin);
  or or_1 (cout, and_1_out, and_2_out, and_3_out);
  or or_2 (s, and_4_out, and_5_out, and_6_out, and_7_out);
endmodule

module half_adder (
  input  a,
  input  b,
  output s,
  output cout
);

  wire and_2_out, and_3_out, not_1_out, not_2_out;

  not not_1 (not_1_out, a);
  not not_2 (not_2_out, b);
  and and_1 (cout, a, b);
  and and_2 (and_2_out, not_1_out, b);
  and and_3 (and_3_out, a, not_2_out);
  or or_1 (s, and_2_out, and_3_out);
endmodule
