// Logisim project ula2.circ as structural Verilog: 8 circuits, main circuit main
module main (
  input  [7:0] in_1,
  input  in_2,
  input  [2:0] in_3,
  output [7:0] out_4
);

  wire and_1_out, and_2_out, and_3_out, and_4_out, and_5_out, and_6_out, and_7_out, and_8_out, and_9_out,
       and_10_out, and_11_out, and_12_out, and_13_out, and_14_out, and_15_out, and_16_out, and_17_out,
       and_18_out, and_19_out, and_20_out, and_21_out, and_22_out, and_23_out, and_24_out, and_25_out,
       and_26_out, and_27_out, and_28_out, and_29_out, and_30_out, and_31_out, and_32_out, and_33_out,
       and_34_out, and_35_out, and_36_out, and_37_out, and_38_out, and_39_out, and_40_out, and_41_out,
       and_42_out, and_43_out, and_44_out, and_45_out, and_46_out, and_47_out, and_48_out, and_49_out,
       and_50_out, and_51_out, and_52_out, and_53_out, and_54_out, and_55_out, and_56_out, and_57_out,
       and_58_out, and_59_out, and_60_out, and_61_out, and_62_out, and_63_out, and_64_out, and_65_out,
       and_66_out, and_67_out, and_68_out, and_69_out, and_70_out, and_71_out, and_72_out, and_73_out,
       and_74_out, and_75_out, and_76_out, and_77_out, and_78_out, and_79_out, and_80_out, d_ff_1_q,
       d_ff_2_q, d_ff_3_q, d_ff_4_q, d_ff_5_q, d_ff_6_q, d_ff_7_q, d_ff_8_q, d_ff_9_q, d_ff_10_q, d_ff_11_q,
       d_ff_12_q, d_ff_13_q, d_ff_14_q, d_ff_15_q, d_ff_16_q, d_ff_17_q, d_ff_18_q, d_ff_19_q, d_ff_20_q,
       d_ff_21_q, d_ff_22_q, d_ff_23_q, d_ff_24_q, d_ff_25_q, d_ff_26_q, d_ff_27_q, d_ff_28_q, d_ff_29_q,
       d_ff_30_q, d_ff_31_q, d_ff_32_q, d_ff_33_q, d_ff_34_q, d_ff_35_q, d_ff_36_q, d_ff_37_q, d_ff_38_q,
       d_ff_39_q, d_ff_40_q, d_ff_41_q, d_ff_42_q, d_ff_43_q, d_ff_44_q, d_ff_45_q, d_ff_46_q, d_ff_47_q,
       d_ff_48_q, d_ff_49_q, d_ff_50_q, d_ff_51_q, d_ff_52_q, d_ff_53_q, d_ff_54_q, d_ff_55_q, d_ff_56_q,
       d_ff_57_q, d_ff_58_q, d_ff_59_q, d_ff_60_q, d_ff_61_q, d_ff_62_q, d_ff_63_q, d_ff_64_q;

  and and_1 (and_1_out, ~in_3[2], ~in_3[1], ~in_3[0]);  // AND_Gate
  and and_2 (and_2_out, ~in_3[2], ~in_3[1], in_3[0]);  // AND_Gate
  and and_3 (and_3_out, ~in_3[2], in_3[1], ~in_3[0]);  // AND_Gate
  and and_4 (and_4_out, ~in_3[2], in_3[1], in_3[0]);  // AND_Gate
  and and_5 (and_5_out, in_3[2], ~in_3[1], ~in_3[0]);  // AND_Gate
  and and_6 (and_6_out, in_3[2], ~in_3[1], in_3[0]);  // AND_Gate
  and and_7 (and_7_out, in_3[2], in_3[1], ~in_3[0]);  // AND_Gate
  and and_8 (and_8_out, in_3[2], in_3[1], in_3[0]);
  and and_9 (and_9_out, and_1_out, in_2);
  and and_10 (and_10_out, and_2_out, in_2);
  and and_11 (and_11_out, and_3_out, in_2);
  and and_12 (and_12_out, and_4_out, in_2);
  and and_13 (and_13_out, and_5_out, in_2);
  and and_14 (and_14_out, and_6_out, in_2);
  and and_15 (and_15_out, and_7_out, in_2);
  and and_16 (and_16_out, and_8_out, in_2);
  D_Flip_Flop d_ff_1 (.clk(and_9_out), .D(in_1[7]), .Q(d_ff_1_q));  // open: Qn, preset, en, reset
  and and_17 (and_17_out, d_ff_1_q, and_1_out);
  D_Flip_Flop d_ff_2 (.clk(and_10_out), .D(in_1[7]), .Q(d_ff_2_q));  // open: Qn, preset, en, reset
  D_Flip_Flop d_ff_3 (.clk(and_11_out), .D(in_1[7]), .Q(d_ff_3_q));  // open: Qn, preset, en, reset
  D_Flip_Flop d_ff_4 (.clk(and_12_out), .D(in_1[7]), .Q(d_ff_4_q));  // open: Qn, preset, en, reset
  D_Flip_Flop d_ff_5 (.clk(and_13_out), .D(in_1[7]), .Q(d_ff_5_q));  // open: Qn, preset, en, reset
  D_Flip_Flop d_ff_6 (.clk(and_14_out), .D(in_1[7]), .Q(d_ff_6_q));  // open: Qn, preset, en, reset
  D_Flip_Flop d_ff_7 (.clk(and_15_out), .D(in_1[7]), .Q(d_ff_7_q));  // open: Qn, preset, en, reset
  D_Flip_Flop d_ff_8 (.clk(and_16_out), .D(in_1[7]), .Q(d_ff_8_q));  // open: Qn, preset, en, reset
  and and_18 (and_18_out, d_ff_2_q, and_2_out);
  and and_19 (and_19_out, d_ff_3_q, and_3_out);
  and and_20 (and_20_out, d_ff_4_q, and_4_out);
  and and_21 (and_21_out, d_ff_5_q, and_5_out);
  and and_22 (and_22_out, d_ff_6_q, and_6_out);
  and and_23 (and_23_out, d_ff_7_q, and_7_out);
  and and_24 (and_24_out, d_ff_8_q, and_8_out);
  or or_1 (out_4[7], and_17_out, and_18_out, and_19_out, and_20_out, and_21_out, and_22_out, and_23_out, and_24_out);
  D_Flip_Flop d_ff_9 (.clk(and_9_out), .D(in_1[6]), .Q(d_ff_9_q));  // open: Qn, preset, en, reset
  D_Flip_Flop d_ff_10 (.clk(and_10_out), .D(in_1[6]), .Q(d_ff_10_q));  // open: Qn, preset, en, reset
  D_Flip_Flop d_ff_11 (.clk(and_11_out), .D(in_1[6]), .Q(d_ff_11_q));  // open: Qn, preset, en, reset
  D_Flip_Flop d_ff_12 (.clk(and_12_out), .D(in_1[6]), .Q(d_ff_12_q));  // open: Qn, preset, en, reset
  D_Flip_Flop d_ff_13 (.clk(and_13_out), .D(in_1[6]), .Q(d_ff_13_q));  // open: Qn, preset, en, reset
  D_Flip_Flop d_ff_14 (.clk(and_14_out), .D(in_1[6]), .Q(d_ff_14_q));  // open: Qn, preset, en, reset
  D_Flip_Flop d_ff_15 (.clk(and_15_out), .D(in_1[6]), .Q(d_ff_15_q));  // open: Qn, preset, en, reset
  D_Flip_Flop d_ff_16 (.clk(and_16_out), .D(in_1[6]), .Q(d_ff_16_q));  // open: Qn, preset, en, reset
  and and_25 (and_25_out, d_ff_9_q, and_1_out);
  and and_26 (and_26_out, d_ff_10_q, and_2_out);
  and and_27 (and_27_out, d_ff_11_q, and_3_out);
  and and_28 (and_28_out, d_ff_12_q, and_4_out);
  and and_29 (and_29_out, d_ff_13_q, and_5_out);
  or or_2 (out_4[6], and_25_out, and_26_out, and_27_out, and_28_out, and_29_out, and_30_out, and_31_out, and_32_out);
  and and_30 (and_30_out, d_ff_14_q, and_6_out);
  and and_31 (and_31_out, d_ff_15_q, and_7_out);
  and and_32 (and_32_out, d_ff_16_q, and_8_out);
  D_Flip_Flop d_ff_17 (.clk(and_9_out), .D(in_1[5]), .Q(d_ff_17_q));  // open: Qn, preset, en, reset
  and and_33 (and_33_out, d_ff_17_q, and_1_out);
  D_Flip_Flop d_ff_18 (.clk(and_10_out), .D(in_1[5]), .Q(d_ff_18_q));  // open: Qn, preset, en, reset
  and and_34 (and_34_out, d_ff_18_q, and_2_out);
  D_Flip_Flop d_ff_19 (.clk(and_11_out), .D(in_1[5]), .Q(d_ff_19_q));  // open: Qn, preset, en, reset
  and and_35 (and_35_out, d_ff_19_q, and_3_out);
  D_Flip_Flop d_ff_20 (.clk(and_12_out), .D(in_1[5]), .Q(d_ff_20_q));  // open: Qn, preset, en, reset
  D_Flip_Flop d_ff_21 (.clk(and_13_out), .D(in_1[5]), .Q(d_ff_21_q));  // open: Qn, preset, en, reset
  D_Flip_Flop d_ff_22 (.clk(and_14_out), .D(in_1[5]), .Q(d_ff_22_q));  // open: Qn, preset, en, reset
  D_Flip_Flop d_ff_23 (.clk(and_15_out), .D(in_1[5]), .Q(d_ff_23_q));  // open: Qn, preset, en, reset
  D_Flip_Flop d_ff_24 (.clk(and_16_out), .D(in_1[5]), .Q(d_ff_24_q));  // open: Qn, preset, en, reset
  and and_36 (and_36_out, d_ff_20_q, and_4_out);
  and and_37 (and_37_out, d_ff_21_q, and_5_out);
  and and_38 (and_38_out, d_ff_22_q, and_6_out);
  and and_39 (and_39_out, d_ff_23_q, and_7_out);
  and and_40 (and_40_out, d_ff_24_q, and_8_out);
  or or_3 (out_4[5], and_33_out, and_34_out, and_35_out, and_36_out, and_37_out, and_38_out, and_39_out, and_40_out);
  D_Flip_Flop d_ff_25 (.clk(and_9_out), .D(in_1[4]), .Q(d_ff_25_q));  // open: Qn, preset, en, reset
  D_Flip_Flop d_ff_26 (.clk(and_10_out), .D(in_1[4]), .Q(d_ff_26_q));  // open: Qn, preset, en, reset
  D_Flip_Flop d_ff_27 (.clk(and_11_out), .D(in_1[4]), .Q(d_ff_27_q));  // open: Qn, preset, en, reset
  D_Flip_Flop d_ff_28 (.clk(and_12_out), .D(in_1[4]), .Q(d_ff_28_q));  // open: Qn, preset, en, reset
  D_Flip_Flop d_ff_29 (.clk(and_13_out), .D(in_1[4]), .Q(d_ff_29_q));  // open: Qn, preset, en, reset
  D_Flip_Flop d_ff_30 (.clk(and_14_out), .D(in_1[4]), .Q(d_ff_30_q));  // open: Qn, preset, en, reset
  D_Flip_Flop d_ff_31 (.clk(and_15_out), .D(in_1[4]), .Q(d_ff_31_q));  // open: Qn, preset, en, reset
  D_Flip_Flop d_ff_32 (.clk(and_16_out), .D(in_1[4]), .Q(d_ff_32_q));  // open: Qn, preset, en, reset
  and and_41 (and_41_out, d_ff_25_q, and_1_out);
  and and_42 (and_42_out, d_ff_26_q, and_2_out);
  and and_43 (and_43_out, d_ff_27_q, and_3_out);
  and and_44 (and_44_out, d_ff_28_q, and_4_out);
  and and_45 (and_45_out, d_ff_29_q, and_5_out);
  and and_46 (and_46_out, d_ff_30_q, and_6_out);
  and and_47 (and_47_out, d_ff_31_q, and_7_out);
  or or_4 (out_4[4], and_41_out, and_42_out, and_43_out, and_44_out, and_45_out, and_46_out, and_47_out, and_48_out);
  and and_48 (and_48_out, d_ff_32_q, and_8_out);
  D_Flip_Flop d_ff_33 (.clk(and_9_out), .D(in_1[3]), .Q(d_ff_33_q));  // open: Qn, preset, en, reset
  and and_49 (and_49_out, d_ff_33_q, and_1_out);
  D_Flip_Flop d_ff_34 (.clk(and_10_out), .D(in_1[3]), .Q(d_ff_34_q));  // open: Qn, preset, en, reset
  and and_50 (and_50_out, d_ff_34_q, and_2_out);
  D_Flip_Flop d_ff_35 (.clk(and_11_out), .D(in_1[3]), .Q(d_ff_35_q));  // open: Qn, preset, en, reset
  and and_51 (and_51_out, d_ff_35_q, and_3_out);
  D_Flip_Flop d_ff_36 (.clk(and_12_out), .D(in_1[3]), .Q(d_ff_36_q));  // open: Qn, preset, en, reset
  and and_52 (and_52_out, d_ff_36_q, and_4_out);
  D_Flip_Flop d_ff_37 (.clk(and_13_out), .D(in_1[3]), .Q(d_ff_37_q));  // open: Qn, preset, en, reset
  and and_53 (and_53_out, d_ff_37_q, and_5_out);
  D_Flip_Flop d_ff_38 (.clk(and_14_out), .D(in_1[3]), .Q(d_ff_38_q));  // open: Qn, preset, en, reset
  D_Flip_Flop d_ff_39 (.clk(and_15_out), .D(in_1[3]), .Q(d_ff_39_q));  // open: Qn, preset, en, reset
  D_Flip_Flop d_ff_40 (.clk(and_16_out), .D(in_1[3]), .Q(d_ff_40_q));  // open: Qn, preset, en, reset
  or or_5 (out_4[3], and_49_out, and_50_out, and_51_out, and_52_out, and_53_out, and_54_out, and_55_out, and_56_out);
  and and_54 (and_54_out, d_ff_38_q, and_6_out);
  and and_55 (and_55_out, d_ff_39_q, and_7_out);
  and and_56 (and_56_out, d_ff_40_q, and_8_out);
  D_Flip_Flop d_ff_41 (.clk(and_9_out), .D(in_1[2]), .Q(d_ff_41_q));  // open: Qn, preset, en, reset
  and and_57 (and_57_out, d_ff_41_q, and_1_out);
  D_Flip_Flop d_ff_42 (.clk(and_10_out), .D(in_1[2]), .Q(d_ff_42_q));  // open: Qn, preset, en, reset
  and and_58 (and_58_out, d_ff_42_q, and_2_out);
  D_Flip_Flop d_ff_43 (.clk(and_11_out), .D(in_1[2]), .Q(d_ff_43_q));  // open: Qn, preset, en, reset
  D_Flip_Flop d_ff_44 (.clk(and_12_out), .D(in_1[2]), .Q(d_ff_44_q));  // open: Qn, preset, en, reset
  D_Flip_Flop d_ff_45 (.clk(and_13_out), .D(in_1[2]), .Q(d_ff_45_q));  // open: Qn, preset, en, reset
  D_Flip_Flop d_ff_46 (.clk(and_14_out), .D(in_1[2]), .Q(d_ff_46_q));  // open: Qn, preset, en, reset
  D_Flip_Flop d_ff_47 (.clk(and_15_out), .D(in_1[2]), .Q(d_ff_47_q));  // open: Qn, preset, en, reset
  D_Flip_Flop d_ff_48 (.clk(and_16_out), .D(in_1[2]), .Q(d_ff_48_q));  // open: Qn, preset, en, reset
  and and_59 (and_59_out, d_ff_43_q, and_3_out);
  and and_60 (and_60_out, d_ff_44_q, and_4_out);
  and and_61 (and_61_out, d_ff_45_q, and_5_out);
  and and_62 (and_62_out, d_ff_46_q, and_6_out);
  and and_63 (and_63_out, d_ff_47_q, and_7_out);
  and and_64 (and_64_out, d_ff_48_q, and_8_out);
  or or_6 (out_4[2], and_57_out, and_58_out, and_59_out, and_60_out, and_61_out, and_62_out, and_63_out, and_64_out);
  D_Flip_Flop d_ff_49 (.clk(and_9_out), .D(in_1[1]), .Q(d_ff_49_q));  // open: Qn, preset, en, reset
  D_Flip_Flop d_ff_50 (.clk(and_10_out), .D(in_1[1]), .Q(d_ff_50_q));  // open: Qn, preset, en, reset
  D_Flip_Flop d_ff_51 (.clk(and_11_out), .D(in_1[1]), .Q(d_ff_51_q));  // open: Qn, preset, en, reset
  D_Flip_Flop d_ff_52 (.clk(and_12_out), .D(in_1[1]), .Q(d_ff_52_q));  // open: Qn, preset, en, reset
  D_Flip_Flop d_ff_53 (.clk(and_13_out), .D(in_1[1]), .Q(d_ff_53_q));  // open: Qn, preset, en, reset
  D_Flip_Flop d_ff_54 (.clk(and_14_out), .D(in_1[1]), .Q(d_ff_54_q));  // open: Qn, preset, en, reset
  D_Flip_Flop d_ff_55 (.clk(and_15_out), .D(in_1[1]), .Q(d_ff_55_q));  // open: Qn, preset, en, reset
  D_Flip_Flop d_ff_56 (.clk(and_16_out), .D(in_1[1]), .Q(d_ff_56_q));  // open: Qn, preset, en, reset
  and and_65 (and_65_out, d_ff_49_q, and_1_out);
  and and_66 (and_66_out, d_ff_50_q, and_2_out);
  and and_67 (and_67_out, d_ff_51_q, and_3_out);
  and and_68 (and_68_out, d_ff_52_q, and_4_out);
  and and_69 (and_69_out, d_ff_53_q, and_5_out);
  and and_70 (and_70_out, d_ff_54_q, and_6_out);
  or or_7 (out_4[1], and_65_out, and_66_out, and_67_out, and_68_out, and_69_out, and_70_out, and_71_out, and_72_out);
  and and_71 (and_71_out, d_ff_55_q, and_7_out);
  and and_72 (and_72_out, d_ff_56_q, and_8_out);
  D_Flip_Flop d_ff_57 (.clk(and_9_out), .D(in_1[0]), .Q(d_ff_57_q));  // open: Qn, preset, en, reset
  and and_73 (and_73_out, d_ff_57_q, and_1_out);
  D_Flip_Flop d_ff_58 (.clk(and_10_out), .D(in_1[0]), .Q(d_ff_58_q));  // open: Qn, preset, en, reset
  and and_74 (and_74_out, d_ff_58_q, and_2_out);
  D_Flip_Flop d_ff_59 (.clk(and_11_out), .D(in_1[0]), .Q(d_ff_59_q));  // open: Qn, preset, en, reset
  and and_75 (and_75_out, d_ff_59_q, and_3_out);
  D_Flip_Flop d_ff_60 (.clk(and_12_out), .D(in_1[0]), .Q(d_ff_60_q));  // open: Qn, preset, en, reset
  and and_76 (and_76_out, d_ff_60_q, and_4_out);
  D_Flip_Flop d_ff_61 (.clk(and_13_out), .D(in_1[0]), .Q(d_ff_61_q));  // open: Qn, preset, en, reset
  D_Flip_Flop d_ff_62 (.clk(and_14_out), .D(in_1[0]), .Q(d_ff_62_q));  // open: Qn, preset, en, reset
  D_Flip_Flop d_ff_63 (.clk(and_15_out), .D(in_1[0]), .Q(d_ff_63_q));  // open: Qn, preset, en, reset
  D_Flip_Flop d_ff_64 (.clk(and_16_out), .D(in_1[0]), .Q(d_ff_64_q));  // open: Qn, preset, en, reset
  or or_8 (out_4[0], and_73_out, and_74_out, and_75_out, and_76_out, and_77_out, and_78_out, and_79_out, and_80_out);
  and and_77 (and_77_out, d_ff_61_q, and_5_out);
  and and_78 (and_78_out, d_ff_62_q, and_6_out);
  and and_79 (and_79_out, d_ff_63_q, and_7_out);
  and and_80 (and_80_out, d_ff_64_q, and_8_out);
endmodule

module teste (
  input  [7:0] in_1,
  input  in_2,
  input  in_3,
  output [2:0] out_4,
  output [7:0] out_5
);

  contando_0_7 contando_0_7_1 (.in_1(in_3), .out_2(out_4));
  main main_1 (.in_1(in_1), .in_3(out_4), .out_4(out_5), .in_2(in_2));
endmodule

module contando_0_7 (
  input  in_1,
  output [2:0] out_2
);

  T_Flip_Flop #(.trigger("falling")) t_ff_1 (.clk(in_1), .T(1'b1), .Q(out_2[0]));  // open: Qn, preset, reset, en
  T_Flip_Flop #(.trigger("falling")) t_ff_2 (.clk(out_2[0]), .T(1'b1), .Q(out_2[1]));  // open: Qn, preset, reset, en
  T_Flip_Flop #(.trigger("falling")) t_ff_3 (.clk(out_2[1]), .T(1'b1), .Q(out_2[2]));  // open: Qn, preset, reset, en
endmodule

module ula (
  input  [7:0] in_1,
  input  [7:0] in_2,
  input  [2:0] in_3,
  output [7:0] out_4
);

  wire and_1_out, and_2_out, and_3_out, and_4_out, and_5_out, and_6_out, and_7_out, and_8_out, not_1_out,
       not_2_out, not_3_out, not_4_out, not_5_out, not_6_out, not_7_out, not_8_out;
  wire [7:0] \and , and_9_out, divisor, divisor_1_out_4, multiplicacao, multiplicador_1_out_3, \nor ,
       nor_1_out, \or , or_1_out, somador, somador_1_out_4, somador_2_out_4, subtracao, \xor , xor_1_out;

  and and_1 (and_1_out, ~in_3[2], ~in_3[1], ~in_3[0]);  // AND_Gate
  and and_2 (and_2_out, ~in_3[2], ~in_3[1], in_3[0]);  // AND_Gate
  and and_3 (and_3_out, ~in_3[2], in_3[1], ~in_3[0]);  // AND_Gate
  and and_4 (and_4_out, ~in_3[2], in_3[1], in_3[0]);  // AND_Gate
  and and_5 (and_5_out, in_3[2], ~in_3[1], ~in_3[0]);  // AND_Gate
  and and_6 (and_6_out, in_3[2], ~in_3[1], in_3[0]);  // AND_Gate
  and and_7 (and_7_out, in_3[2], in_3[1], ~in_3[0]);  // AND_Gate
  and and_8 (and_8_out, in_3[2], in_3[1], in_3[0]);
  assign and_9_out = in_2 & in_1;  // AND_Gate and_9, 8 bits wide
  not not_1 (not_1_out, and_1_out);
  somador somador_1 (.in_3(1'b0), .in_1(in_1), .in_2(in_2), .out_4(somador_1_out_4));  // open: out_5
  not not_2 (not_2_out, and_3_out);
  somador somador_2 (.in_3(1'b1), .in_1(in_1), .in_2(in_2), .out_4(somador_2_out_4));  // open: out_5
  not not_3 (not_3_out, and_4_out);
  multiplicador multiplicador_1 (.in_1(in_1), .in_2(in_2), .out_3(multiplicador_1_out_3));
  not not_4 (not_4_out, and_5_out);
  divisor divisor_1 (.in_1(in_2), .in_2(in_1), .out_4(divisor_1_out_4));  // open: out_3
  not not_5 (not_5_out, and_6_out);
  assign xor_1_out = in_1 ^ in_2;  // XOR_Gate xor_1, 8 bits wide
  not not_6 (not_6_out, and_7_out);
  assign nor_1_out = ~(in_1 | in_2);  // NOR_Gate nor_1, 8 bits wide
  not not_7 (not_7_out, and_8_out);
  Multiplexer #(.width(8)) multiplexer_1 (.in0(and_9_out), .in1({8{1'b0}}), .out(\and ), .sel(not_1_out));  // open: en
  assign or_1_out = in_2 | in_1;  // OR_Gate or_1, 8 bits wide
  Multiplexer #(.width(8)) multiplexer_2 (.in0(or_1_out), .in1({8{1'b0}}), .out(\or ), .sel(not_8_out));  // open: en
  not not_8 (not_8_out, and_2_out);
  Multiplexer #(.width(8)) multiplexer_3 (
    .in0(somador_1_out_4), .in1({8{1'b0}}), .out(somador), .sel(not_2_out));  // open: en
  Multiplexer #(.width(8)) multiplexer_4 (
    .in0(somador_2_out_4), .in1({8{1'b0}}), .out(subtracao), .sel(not_3_out));  // open: en
  Multiplexer #(.width(8)) multiplexer_5 (
    .in0(multiplicador_1_out_3), .in1({8{1'b0}}), .out(multiplicacao), .sel(not_4_out));  // open: en
  Multiplexer #(.width(8)) multiplexer_6 (
    .in0(divisor_1_out_4), .in1({8{1'b0}}), .out(divisor), .sel(not_5_out));  // open: en
  Multiplexer #(.width(8)) multiplexer_7 (.in0(xor_1_out), .in1({8{1'b0}}), .out(\xor ), .sel(not_6_out));  // open: en
  Multiplexer #(.width(8)) multiplexer_8 (.in0(nor_1_out), .in1({8{1'b0}}), .out(\nor ), .sel(not_7_out));  // open: en
  assign out_4 = \nor  | \xor  | \and  | \or  | somador | subtracao | multiplicacao | divisor;  // OR_Gate or_2, 8 bits wide

  // Other names for the same wires on the sheet: A[7:0] = in_1; B[7:0] = in_2; saida[7:0] = out_4
endmodule

module sistema (
  input  [7:0] in_1,
  input  [7:0] in_2,
  input  in_3,
  input  [2:0] in_4,
  input  [2:0] in_5,
  output [7:0] out_6
);

  wire [7:0] ula_1_out_4;

  ula ula_1 (.in_1(in_1), .in_2(in_2), .in_3(in_4), .out_4(ula_1_out_4));
  main main_1 (.in_1(ula_1_out_4), .in_3(in_5), .out_4(out_6), .in_2(in_3));
endmodule

module somador (
  input  [7:0] in_1,
  input  [7:0] in_2,
  input  in_3,
  output [7:0] out_4,
  output out_5
);

  wire and_1_out, and_2_out, and_3_out, and_4_out, and_5_out, and_6_out, and_7_out, and_8_out, and_9_out,
       and_10_out, and_11_out, and_12_out, and_13_out, and_14_out, and_15_out, and_16_out, and_17_out,
       and_18_out, and_19_out, and_20_out, and_21_out, and_22_out, and_23_out, and_24_out, and_25_out,
       and_26_out, and_27_out, and_28_out, and_29_out, and_30_out, and_31_out, and_32_out, and_33_out,
       and_34_out, and_35_out, or_1_out, or_2_out, or_3_out, or_4_out, or_5_out, or_6_out, or_7_out,
       or_8_out, or_9_out, or_10_out, or_11_out, or_12_out, or_13_out, or_14_out;
  wire [7:0] xor_1_out;

  assign xor_1_out = in_2 ^ {8{in_3}};  // XOR_Gate xor_1, 8 bits wide
  divisor_main main_1 (.a(xor_1_out[0]), .b(in_1[0]), .c(in_3), .y(out_4[0]));
  and and_1 (and_1_out, in_1[0], xor_1_out[0]);
  or or_1 (or_1_out, in_1[0], xor_1_out[0]);
  and and_2 (and_2_out, or_1_out, in_3);
  or or_2 (or_2_out, and_1_out, and_2_out);
  divisor_main main_2 (.a(xor_1_out[1]), .b(in_1[1]), .c(or_2_out), .y(out_4[1]));
  and and_3 (and_3_out, in_1[1], xor_1_out[1]);
  and and_4 (and_4_out, and_1_out, or_4_out);
  or or_3 (or_3_out, and_3_out, and_4_out, and_5_out);
  divisor_main main_3 (.a(xor_1_out[2]), .b(in_1[2]), .c(or_3_out), .y(out_4[2]));
  or or_4 (or_4_out, in_1[1], xor_1_out[1]);
  and and_5 (and_5_out, or_1_out, or_4_out, in_3);
  divisor_main main_4 (.a(xor_1_out[3]), .b(in_1[3]), .c(or_6_out), .y(out_4[3]));
  and and_6 (and_6_out, in_1[2], xor_1_out[2]);
  or or_5 (or_5_out, in_1[2], xor_1_out[2]);
  and and_7 (and_7_out, and_1_out, or_4_out, or_5_out);
  and and_8 (and_8_out, and_3_out, or_5_out);
  or or_6 (or_6_out, and_6_out, and_8_out, and_7_out, and_9_out);
  and and_9 (and_9_out, in_3, or_1_out, or_4_out, or_5_out);
  divisor_main main_5 (.a(xor_1_out[4]), .b(in_1[4]), .c(or_8_out), .y(out_4[4]));
  and and_10 (and_10_out, in_1[3], xor_1_out[3]);
  or or_7 (or_7_out, in_1[3], xor_1_out[3]);
  and and_11 (and_11_out, and_6_out, or_7_out);
  and and_12 (and_12_out, and_3_out, or_5_out, or_7_out);
  or or_8 (or_8_out, and_10_out, and_11_out, and_12_out, and_14_out, and_13_out);
  and and_13 (and_13_out, in_3, or_1_out, or_4_out, or_5_out, or_7_out);
  and and_14 (and_14_out, and_1_out, and_3_out, and_6_out, or_7_out);
  and and_15 (and_15_out, in_1[4], xor_1_out[4]);
  and and_16 (and_16_out, and_10_out, or_9_out);
  divisor_main main_6 (.a(xor_1_out[5]), .b(in_1[5]), .c(or_10_out), .y(out_4[5]));
  or or_9 (or_9_out, in_1[4], xor_1_out[4]);
  and and_17 (and_17_out, and_6_out, or_7_out, or_9_out);
  and and_18 (and_18_out, and_3_out, or_5_out, or_7_out, or_9_out);
  or or_10 (or_10_out, and_15_out, and_16_out, and_17_out, and_18_out, and_19_out, and_20_out);
  and and_19 (and_19_out, and_1_out, and_3_out, and_6_out, and_10_out, and_15_out);
  and and_20 (and_20_out, in_3, or_1_out, or_4_out, or_5_out, or_7_out, or_9_out);
  divisor_main main_7 (.a(xor_1_out[6]), .b(in_1[6]), .c(or_12_out), .y(out_4[6]));
  or or_11 (or_11_out, in_1[5], xor_1_out[5]);
  and and_21 (and_21_out, in_1[5], xor_1_out[5]);
  and and_22 (and_22_out, and_10_out, or_9_out, or_11_out);
  and and_23 (and_23_out, and_15_out, or_11_out);
  or or_12 (or_12_out, and_21_out, and_23_out, and_22_out, and_25_out, and_24_out, and_26_out, and_27_out);
  and and_24 (and_24_out, and_3_out, or_5_out, or_7_out, or_9_out, or_11_out);
  and and_25 (and_25_out, and_6_out, or_7_out, or_9_out, or_11_out);
  and and_26 (and_26_out, and_1_out, and_3_out, and_6_out, and_10_out, and_15_out, and_21_out);
  and and_27 (and_27_out, in_3, or_1_out, or_4_out, or_5_out, or_7_out, or_9_out, or_11_out);
  or or_13 (or_13_out, in_1[6], xor_1_out[6]);
  and and_28 (and_28_out, in_1[6], xor_1_out[6]);
  and and_29 (and_29_out, and_21_out, or_13_out);
  divisor_main main_8 (.a(xor_1_out[7]), .b(in_1[7]), .c(or_14_out), .y(out_4[7]));
  and and_30 (and_30_out, and_10_out, or_9_out, or_11_out, or_13_out);
  and and_31 (and_31_out, and_15_out, or_11_out, or_13_out);
  or or_14 (or_14_out, and_28_out, and_29_out, and_31_out, and_30_out, and_32_out, and_34_out, and_33_out, and_35_out);
  and and_32 (and_32_out, and_6_out, or_7_out, or_9_out, or_11_out, or_13_out);
  and and_33 (and_33_out, and_3_out, and_3_out, or_5_out, or_7_out, or_9_out, or_11_out, or_13_out);
  and and_34 (and_34_out, and_3_out, and_6_out, and_10_out, and_15_out, and_21_out, and_28_out);
  and and_35 (and_35_out, in_3, or_1_out, or_4_out, or_5_out, or_7_out, or_9_out, or_11_out, or_13_out);

  assign out_5 = out_4[7];
endmodule

module divisor (
  input  [7:0] in_1,
  input  [7:0] in_2,
  output [7:0] out_3,
  output [7:0] out_4
);

  wire s0, s1, s2, s3, s4, s5, s6, s7;
  wire [7:0] multiplexer_1_out, multiplexer_2_out, multiplexer_3_out, multiplexer_4_out, multiplexer_5_out,
       multiplexer_6_out, multiplexer_7_out, somador_1_out_4, somador_2_out_4, somador_3_out_4,
       somador_4_out_4, somador_5_out_4, somador_6_out_4, somador_7_out_4, somador_8_out_4;

  divisor_1__somador somador_1 (
    .in_3(1'b1), .out_5(s7), .in_1({{7{1'b0}}, in_2[7]}), .in_2(in_1), .out_4(somador_1_out_4));
  Multiplexer #(.width(8)) multiplexer_1 (
    .in0(somador_1_out_4), .in1({{7{1'b0}}, in_2[7]}), .out(multiplexer_1_out), .sel(s7));  // open: en
  not not_1 (out_4[6], s6);
  not not_2 (out_4[5], s5);
  not not_3 (out_4[7], s7);
  not not_4 (out_4[3], s3);
  not not_5 (out_4[4], s4);
  divisor_1__somador somador_2 (
    .in_3(1'b1), .out_5(s6), .in_1({multiplexer_1_out[6:0], in_2[6]}), .in_2(in_1), .out_4(somador_2_out_4));
  not not_6 (out_4[1], s1);
  not not_7 (out_4[2], s2);
  not not_8 (out_4[0], s0);
  Multiplexer #(.width(8)) multiplexer_2 (
    .in0(somador_2_out_4), .in1({multiplexer_1_out[6:0], in_2[6]}), .out(multiplexer_2_out), .sel(s6));  // open: en
  divisor_1__somador somador_3 (
    .in_3(1'b1), .out_5(s5), .in_1({multiplexer_2_out[6:0], in_2[5]}), .in_2(in_1), .out_4(somador_3_out_4));
  Multiplexer #(.width(8)) multiplexer_3 (
    .in0(somador_3_out_4), .in1({multiplexer_2_out[6:0], in_2[5]}), .out(multiplexer_3_out), .sel(s5));  // open: en
  divisor_1__somador somador_4 (
    .in_3(1'b1), .out_5(s4), .in_1({multiplexer_3_out[6:0], in_2[4]}), .in_2(in_1), .out_4(somador_4_out_4));
  Multiplexer #(.width(8)) multiplexer_4 (
    .in0(somador_4_out_4), .in1({multiplexer_3_out[6:0], in_2[4]}), .out(multiplexer_4_out), .sel(s4));  // open: en
  divisor_1__somador somador_5 (
    .in_3(1'b1), .out_5(s3), .in_1({multiplexer_4_out[6:0], in_2[3]}), .in_2(in_1), .out_4(somador_5_out_4));
  Multiplexer #(.width(8)) multiplexer_5 (
    .in0(somador_5_out_4), .in1({multiplexer_4_out[6:0], in_2[3]}), .out(multiplexer_5_out), .sel(s3));  // open: en
  divisor_1__somador somador_6 (
    .in_3(1'b1), .out_5(s2), .in_1({multiplexer_5_out[6:0], in_2[2]}), .in_2(in_1), .out_4(somador_6_out_4));
  Multiplexer #(.width(8)) multiplexer_6 (
    .in0(somador_6_out_4), .in1({multiplexer_5_out[6:0], in_2[2]}), .out(multiplexer_6_out), .sel(s2));  // open: en
  divisor_1__somador somador_7 (
    .in_3(1'b1), .out_5(s1), .in_1({multiplexer_6_out[6:0], in_2[1]}), .in_2(in_1), .out_4(somador_7_out_4));
  Multiplexer #(.width(8)) multiplexer_7 (
    .in0(somador_7_out_4), .in1({multiplexer_6_out[6:0], in_2[1]}), .out(multiplexer_7_out), .sel(s1));  // open: en
  divisor_1__somador somador_8 (
    .in_3(1'b1), .out_5(s0), .in_1({multiplexer_7_out[6:0], in_2[0]}), .in_2(in_1), .out_4(somador_8_out_4));
  Multiplexer #(.width(8)) multiplexer_8 (
    .in0(somador_8_out_4), .in1({multiplexer_7_out[6:0], in_2[0]}), .out(out_3), .sel(s0));  // open: en

  // Other names for the same wires on the sheet: dividendo[7:0] = in_2; divisor[7:0] = in_1; quociente[7:0] = out_4;
  //   saida[7:0] = out_3
endmodule

module multiplicador (
  input  [7:0] in_1,
  input  [7:0] in_2,
  output [7:0] out_3
);

  wire and_1_out, and_2_out, and_3_out, and_4_out, and_5_out, and_6_out, and_7_out, and_8_out, and_9_out,
       and_10_out, and_11_out, and_12_out, and_13_out, and_14_out, and_15_out, and_16_out, and_17_out,
       and_18_out, and_19_out, and_20_out, and_21_out, and_22_out, and_23_out, and_24_out, and_25_out,
       and_26_out, and_27_out, and_28_out, and_29_out, and_30_out, and_31_out, and_32_out, and_33_out,
       and_34_out, and_35_out, full_adder_1_cout, full_adder_1_s, full_adder_2_cout, full_adder_2_s,
       full_adder_3_cout, full_adder_3_s, full_adder_4_cout, full_adder_4_s, full_adder_5_cout,
       full_adder_5_s, full_adder_6_cout, full_adder_6_s, full_adder_7_cout, full_adder_7_s,
       full_adder_8_cout, full_adder_8_s, full_adder_9_cout, full_adder_9_s, full_adder_10_cout,
       full_adder_10_s, full_adder_11_cout, full_adder_11_s, full_adder_12_cout, full_adder_12_s,
       full_adder_13_cout, full_adder_13_s, full_adder_14_cout, full_adder_14_s, full_adder_15_cout,
       full_adder_15_s, full_adder_16_cout, full_adder_16_s, full_adder_17_cout, full_adder_17_s,
       full_adder_18_cout, full_adder_18_s, full_adder_19_cout, full_adder_19_s, full_adder_20_cout,
       full_adder_20_s, full_adder_21_cout, full_adder_21_s, half_adder_1_cout, half_adder_2_cout,
       half_adder_3_cout, half_adder_4_cout, half_adder_5_cout, half_adder_6_cout, half_adder_7_cout;
  wire [3:3] undriven;

  Hex_Digit_Display hex_digit_display_1 (.value({undriven[3], in_1[2:0]}));  // open: dp
  Hex_Digit_Display hex_digit_display_2 (.value({1'b0, in_2[2:0]}));  // open: dp
  and and_1 (and_1_out, in_1[7], in_2[0]);
  and and_2 (and_2_out, in_1[6], in_2[1]);
  Full_adder full_adder_1 (
    .a(and_2_out), .b(and_1_out), .cin(full_adder_7_cout), .s(full_adder_1_s), .cout(full_adder_1_cout));
  and and_3 (and_3_out, in_1[5], in_2[2]);
  Full_adder full_adder_2 (
    .a(and_3_out), .b(full_adder_1_s), .cin(full_adder_8_cout), .s(full_adder_2_s), .cout(full_adder_2_cout));
  and and_4 (and_4_out, in_1[4], in_2[3]);
  Full_adder full_adder_3 (
    .a(and_4_out), .b(full_adder_2_s), .cin(full_adder_9_cout), .s(full_adder_3_s), .cout(full_adder_3_cout));
  and and_5 (and_5_out, in_1[3], in_2[4]);
  Full_adder full_adder_4 (
    .a(and_5_out), .b(full_adder_3_s), .cin(full_adder_10_cout), .s(full_adder_4_s), .cout(full_adder_4_cout));
  and and_6 (and_6_out, in_1[2], in_2[5]);
  Full_adder full_adder_5 (
    .a(and_6_out), .b(full_adder_4_s), .cin(full_adder_11_cout), .s(full_adder_5_s), .cout(full_adder_5_cout));
  and and_7 (and_7_out, in_1[1], in_2[6]);
  Full_adder full_adder_6 (
    .a(and_7_out), .b(full_adder_5_s), .cin(half_adder_2_cout), .s(full_adder_6_s), .cout(full_adder_6_cout));
  and and_8 (and_8_out, in_1[0], in_2[7]);
  half_adder half_adder_1 (.a(and_8_out), .b(full_adder_6_s), .s(out_3[7]), .cout(half_adder_1_cout));
  and and_9 (and_9_out, in_1[6], in_2[0]);
  and and_10 (and_10_out, in_1[5], in_2[1]);
  Full_adder full_adder_7 (
    .a(and_10_out), .b(and_9_out), .cin(full_adder_12_cout), .s(full_adder_7_s), .cout(full_adder_7_cout));
  and and_11 (and_11_out, in_1[4], in_2[2]);
  Full_adder full_adder_8 (
    .a(and_11_out), .b(full_adder_7_s), .cin(full_adder_13_cout), .s(full_adder_8_s), .cout(full_adder_8_cout));
  and and_12 (and_12_out, in_1[3], in_2[3]);
  Full_adder full_adder_9 (
    .a(and_12_out), .b(full_adder_8_s), .cin(full_adder_14_cout), .s(full_adder_9_s), .cout(full_adder_9_cout));
  and and_13 (and_13_out, in_1[2], in_2[4]);
  Full_adder full_adder_10 (
    .a(and_13_out), .b(full_adder_9_s), .cin(full_adder_15_cout), .s(full_adder_10_s),
    .cout(full_adder_10_cout));
  and and_14 (and_14_out, in_1[1], in_2[5]);
  Full_adder full_adder_11 (
    .a(and_14_out), .b(full_adder_10_s), .cin(half_adder_3_cout), .s(full_adder_11_s),
    .cout(full_adder_11_cout));
  and and_15 (and_15_out, in_1[0], in_2[6]);
  half_adder half_adder_2 (.a(and_15_out), .b(full_adder_11_s), .s(out_3[6]), .cout(half_adder_2_cout));
  and and_16 (and_16_out, in_1[5], in_2[0]);
  and and_17 (and_17_out, in_1[4], in_2[0]);
  and and_18 (and_18_out, in_1[3], in_2[1]);
  and and_19 (and_19_out, in_1[4], in_2[1]);
  Full_adder full_adder_12 (
    .a(and_19_out), .b(and_16_out), .cin(full_adder_16_cout), .s(full_adder_12_s), .cout(full_adder_12_cout));
  and and_20 (and_20_out, in_1[3], in_2[2]);
  and and_21 (and_21_out, in_1[2], in_2[2]);
  Full_adder full_adder_13 (
    .a(and_20_out), .b(full_adder_12_s), .cin(full_adder_17_cout), .s(full_adder_13_s),
    .cout(full_adder_13_cout));
  and and_22 (and_22_out, in_1[2], in_2[3]);
  Full_adder full_adder_14 (
    .a(and_22_out), .b(full_adder_13_s), .cin(full_adder_18_cout), .s(full_adder_14_s),
    .cout(full_adder_14_cout));
  and and_23 (and_23_out, in_1[1], in_2[4]);
  Full_adder full_adder_15 (
    .a(and_23_out), .b(full_adder_14_s), .cin(half_adder_4_cout), .s(full_adder_15_s),
    .cout(full_adder_15_cout));
  and and_24 (and_24_out, in_1[0], in_2[5]);
  half_adder half_adder_3 (.a(and_24_out), .b(full_adder_15_s), .s(out_3[5]), .cout(half_adder_3_cout));
  and and_25 (and_25_out, in_1[3], in_2[0]);
  and and_26 (and_26_out, in_1[2], in_2[1]);
  Full_adder full_adder_16 (
    .a(and_18_out), .b(and_17_out), .cin(full_adder_20_cout), .s(full_adder_16_s), .cout(full_adder_16_cout));
  and and_27 (and_27_out, in_1[1], in_2[2]);
  Full_adder full_adder_17 (
    .a(and_21_out), .b(full_adder_16_s), .cin(full_adder_21_cout), .s(full_adder_17_s),
    .cout(full_adder_17_cout));
  and and_28 (and_28_out, in_1[0], in_2[3]);
  and and_29 (and_29_out, in_1[1], in_2[3]);
  Full_adder full_adder_18 (
    .a(and_29_out), .b(full_adder_17_s), .cin(half_adder_6_cout), .s(full_adder_18_s),
    .cout(full_adder_18_cout));
  and and_30 (and_30_out, in_1[0], in_2[4]);
  half_adder half_adder_4 (.a(and_30_out), .b(full_adder_18_s), .s(out_3[4]), .cout(half_adder_4_cout));
  and and_31 (and_31_out, in_1[2], in_2[0]);
  and and_32 (and_32_out, in_1[1], in_2[1]);
  Full_adder full_adder_19 (
    .a(and_32_out), .b(and_31_out), .cin(half_adder_7_cout), .s(full_adder_19_s), .cout(full_adder_19_cout));
  Full_adder full_adder_20 (
    .a(and_26_out), .b(and_25_out), .cin(full_adder_19_cout), .s(full_adder_20_s), .cout(full_adder_20_cout));
  and and_33 (and_33_out, in_1[0], in_2[2]);
  half_adder half_adder_5 (.a(and_33_out), .b(full_adder_19_s), .s(out_3[2]), .cout(half_adder_5_cout));
  Full_adder full_adder_21 (
    .a(and_27_out), .b(full_adder_20_s), .cin(half_adder_5_cout), .s(full_adder_21_s),
    .cout(full_adder_21_cout));
  half_adder half_adder_6 (.a(and_28_out), .b(full_adder_21_s), .s(out_3[3]), .cout(half_adder_6_cout));
  and and_34 (and_34_out, in_1[1], in_2[0]);
  and and_35 (and_35_out, in_1[0], in_2[1]);
  half_adder half_adder_7 (.a(and_35_out), .b(and_34_out), .s(out_3[1]), .cout(half_adder_7_cout));
  and and_36 (out_3[0], in_1[0], in_2[0]);

  // Other names for the same wires on the sheet: a0 = in_1[0]; a1 = in_1[1]; a2 = in_1[2]; a3 = in_1[3]; a4 = in_1[4];
  //   a5 = in_1[5]; a6 = in_1[6]; a7 = in_1[7]; b0 = in_2[0]; b1 = in_2[1]; b2 = in_2[2]; b3 = in_2[3]; b4 = in_2[4];
  //   b5 = in_2[5]; b6 = in_2[6]; b7 = in_2[7]
endmodule
